// Logisim project 2_Sychcronous-4-bit-UP-counter (1).circ as structural Verilog: 1 circuit, main circuit main
module main (
  output out_1,
  output out_2,
  output out_3,
  output out_4
);

  wire and_1_out, and_2_out, clock_1_out;

  Clock clock_1 (.out(clock_1_out));
  T_Flip_Flop #(.trigger("falling")) t_ff_1 (.clk(clock_1_out), .T(1'b1), .Q(out_4));  // open: Qn, preset, reset, en
  T_Flip_Flop #(.trigger("falling")) t_ff_2 (.clk(clock_1_out), .T(out_4), .Q(out_3));  // open: Qn, preset, reset, en
  and and_1 (and_1_out, out_4, out_3);
  T_Flip_Flop #(.trigger("falling")) t_ff_3 (
    .clk(clock_1_out), .T(and_1_out), .Q(out_2));  // open: Qn, preset, reset, en
  and and_2 (and_2_out, out_4, out_3, out_2);
  T_Flip_Flop #(.trigger("falling")) t_ff_4 (
    .clk(clock_1_out), .T(and_2_out), .Q(out_1));  // open: Qn, preset, reset, en
endmodule
