// Logisim project 4_Asynchronous-counters-using-the-inverted-output.circ as structural Verilog: 1 circuit, main circuit main
module main (
  output out_1,
  output out_2,
  output out_3,
  output out_4,
  output out_5,
  output out_6
);

  wire clock_1_out, clock_2_out, t_ff_3_qn, t_ff_4_qn, t_ff_5_qn, t_ff_6_qn;

  Clock clock_1 (.out(clock_1_out));
  Clock clock_2 (.out(clock_2_out));
  T_Flip_Flop t_ff_1 (.clk(t_ff_3_qn), .T(1'b1), .Q(out_1));  // open: Qn, preset, reset, en
  T_Flip_Flop #(.trigger("falling")) t_ff_2 (.clk(t_ff_4_qn), .T(1'b1), .Q(out_4));  // open: Qn, preset, reset, en
  T_Flip_Flop t_ff_3 (.clk(t_ff_5_qn), .T(1'b1), .Q(out_2), .Qn(t_ff_3_qn));  // open: preset, reset, en
  T_Flip_Flop #(.trigger("falling")) t_ff_4 (
    .clk(t_ff_6_qn), .T(1'b1), .Q(out_5), .Qn(t_ff_4_qn));  // open: preset, reset, en
  T_Flip_Flop t_ff_5 (.clk(clock_1_out), .T(1'b1), .Q(out_3), .Qn(t_ff_5_qn));  // open: preset, reset, en
  T_Flip_Flop #(.trigger("falling")) t_ff_6 (
    .clk(clock_2_out), .T(1'b1), .Q(out_6), .Qn(t_ff_6_qn));  // open: preset, reset, en

  // Notes on the sheet:
  //   Rising Edge
  //   Falling Edge
endmodule
