// Logisim project 5_Ring-Counter.circ as structural Verilog: 1 circuit, main circuit main
module main (
  input  in_1,
  output out_2,
  output out_3,
  output out_4,
  output out_5
);

  wire button_1_out, clock_1_out, or_1_out;

  Button button_1 (.out(button_1_out));
  or or_1 (or_1_out, out_5, button_1_out);
  Clock clock_1 (.out(clock_1_out));
  D_Flip_Flop d_ff_1 (.clk(clock_1_out), .D(or_1_out), .Q(out_2), .en(in_1));  // open: Qn, preset, reset
  D_Flip_Flop d_ff_2 (.clk(clock_1_out), .D(out_2), .Q(out_3), .en(in_1));  // open: Qn, preset, reset
  D_Flip_Flop d_ff_3 (.clk(clock_1_out), .D(out_3), .Q(out_4), .en(in_1));  // open: Qn, preset, reset
  D_Flip_Flop d_ff_4 (.clk(clock_1_out), .D(out_4), .Q(out_5), .en(in_1));  // open: Qn, preset, reset
endmodule
