// Logisim project 7_Synchronous-UP_DOWN-counter.circ as structural Verilog: 1 circuit, main circuit main
module main (
  input  in_1,
  output out_2,
  output out_3,
  output out_4
);

  wire and_1_out, and_2_out, and_3_out, and_4_out, clock_1_out, not_1_out, or_1_out, or_2_out, t_ff_1_qn,
       t_ff_2_qn;

  Clock clock_1 (.out(clock_1_out));
  not not_1 (not_1_out, in_1);
  T_Flip_Flop #(.trigger("falling")) t_ff_1 (
    .clk(clock_1_out), .T(1'b1), .Q(out_4), .Qn(t_ff_1_qn));  // open: preset, reset, en
  and and_1 (and_1_out, in_1, out_4);
  and and_2 (and_2_out, t_ff_1_qn, not_1_out);
  or or_1 (or_1_out, and_1_out, and_2_out);
  T_Flip_Flop #(.trigger("falling")) t_ff_2 (
    .clk(clock_1_out), .T(or_1_out), .Q(out_3), .Qn(t_ff_2_qn));  // open: preset, reset, en
  and and_3 (and_3_out, in_1, out_4, out_3);
  and and_4 (and_4_out, t_ff_2_qn, t_ff_1_qn, not_1_out);
  or or_2 (or_2_out, and_3_out, and_4_out);
  T_Flip_Flop #(.trigger("falling")) t_ff_3 (
    .clk(clock_1_out), .T(or_2_out), .Q(out_2));  // open: Qn, preset, reset, en
endmodule
