// Logisim project 8_Presettable-counters.circ as structural Verilog: 1 circuit, main circuit main
module main (
  input  in_1,
  input  in_2,
  input  in_3,
  input  in_4,
  output out_5,
  output out_6,
  output out_7
);

  wire and_1_out, clock_1_out, nand_1_out, nand_2_out, nand_3_out, nand_4_out, nand_5_out, nand_6_out,
       not_1_out, not_2_out, not_3_out, not_4_out, not_5_out, not_6_out, not_7_out, not_8_out, not_9_out,
       not_10_out;

  Clock clock_1 (.out(clock_1_out));
  not not_1 (not_1_out, nand_1_out);
  not not_2 (not_2_out, in_1);
  not not_3 (not_3_out, in_4);
  nand nand_1 (nand_1_out, in_1, not_3_out);
  T_Flip_Flop t_ff_1 (.clk(clock_1_out), .T(1'b1), .Q(out_7), .preset(not_1_out), .reset(not_4_out));  // open: Qn, en
  not not_4 (not_4_out, nand_2_out);
  nand nand_2 (nand_2_out, not_2_out, not_3_out);
  nand nand_3 (nand_3_out, in_2, not_3_out);
  T_Flip_Flop t_ff_2 (.clk(clock_1_out), .T(out_7), .Q(out_6), .preset(not_6_out), .reset(not_5_out));  // open: Qn, en
  not not_5 (not_5_out, nand_4_out);
  not not_6 (not_6_out, nand_3_out);
  nand nand_4 (nand_4_out, not_7_out, not_3_out);
  not not_7 (not_7_out, in_2);
  and and_1 (and_1_out, out_7, out_6);
  nand nand_5 (nand_5_out, in_3, not_3_out);
  T_Flip_Flop t_ff_3 (
    .clk(clock_1_out), .T(and_1_out), .Q(out_5), .preset(not_8_out), .reset(not_9_out));  // open: Qn, en
  not not_8 (not_8_out, nand_5_out);
  not not_9 (not_9_out, nand_6_out);
  nand nand_6 (nand_6_out, not_10_out, not_3_out);
  not not_10 (not_10_out, in_3);
endmodule
